// Digital circuit bleh.dig as structural Verilog
module bleh (
  input  C,
  input  [3:0] in_2
);

  wire ALU_H_QC, ALU_H_QZ, ALU_L_QC, ALU_L_QZ, ALU_Q_CF, ALU_Q_IO_OE, ALU_Q_OF, ALU_Q_ZF, C0_CE_M, C1_LD_O,
       C2_LD_S, C3_LD_RS, C4_ALU_OP4_LD_IO, C5_LS_ALU_Q_HALT, C_EXEC, C_nEXEC, C_nLD_MEM, C_Q0, C_Q1, C_Q2,
       C_Q3, C_Q4_ALU_OP4, C_Q5_ALU_OP5, C_Q6_OE_IO, CF, comparator_1_eq, IO_PORT_LD_pin9, IO_PORT_LD_pin10,
       IO_PORT_LD_pin11, IO_PORT_LD_pin12, IO_PORT_OE_pin9, IO_PORT_OE_pin10, IO_PORT_OE_pin11,
       IO_PORT_OE_pin12, IO_PORT_OE_pin13, jk_ff_as_1_nq, LD_MEM, MH_2_pin15, MH_pin15, ML_2_pin15, ML_pin15,
       nA15_nEN_RAM, nHALT, nLD_C, nLD_IO, nLD_LS, nLD_MH, nLD_ML, nLD_O, nLD_PORT0, nLD_PORT1, nLD_PORT2,
       nLD_RS, nLD_S, nOE_ALU, nOE_MEM, nOE_MH, nOE_ML, nOE_PORT0, nOE_PORT1, not_1_out, not_2_out,
       not_3_out, not_4_out, nR, OF, or_1_out, or_2_out, or_3_out, PROGRAM_IO_DEV_av, SEL_nM_C, SF,
       TOGGLE_nM_C, ZF;
  wire [3:0] ALU_H_Q, ALU_L_Q, S;
  wire [7:0] BUS, LS, MH, ML, O, PROGRAM_d, RAM_q, register_1_q, RS;
  wire [15:0] A;

  Comparator #(.Bits(4)) comparator_1 (.a(S), .b(4'b0001), .eq(comparator_1_eq));  // open: gt, lt
  JK_FF_AS jk_ff_as_1 (.Set(1'b0), .J(~nHALT), .C(C), .K(~nHALT), .Clr(~nR), .nQ(jk_ff_as_1_nq));  // open: Q
  _74107 PH (
    .pin1(1'b1), .pin2(C_nEXEC), .pin3(C_EXEC), .pin4(nHALT), .pin5(SEL_nM_C), .pin7(1'b0),
    .pin8(TOGGLE_nM_C), .pin9(C_EXEC), .pin10(nR), .pin11(TOGGLE_nM_C), .pin12(C), .pin13(nR), .pin14(1'b1));  // open: pin6
  Break #(.Cycles(200000)) break_1 (.brk(comparator_1_eq));
  Break #(.Cycles(200000)) break_2 (.brk(jk_ff_as_1_nq));
  Reset reset_1 (.out(nR));
  ROM #(.AddrBits(17), .Bits(8)) CTRL_L (
    .A({S[2:1], S[3], SF, S[0], ZF, 1'b0, CF, OF, O}), .sel(1'b1),
    .D({TOGGLE_nM_C, nLD_C, C5_LS_ALU_Q_HALT, C4_ALU_OP4_LD_IO, C3_LD_RS, C2_LD_S, C1_LD_O, C0_CE_M}));
  ROM #(.AddrBits(17), .Bits(8)) CTRL_H (
    .A({S[2:1], S[3], SF, S[0], ZF, 1'b1, CF, OF, O}), .sel(1'b1),
    .D({nOE_MEM, nOE_ALU, nOE_MH, nOE_ML, nLD_MH, nLD_ML, nLD_LS, LD_MEM}));
  _74161 u_S (
    .pin1(nR), .pin2(C_nEXEC), .pin3(1'b0), .pin4(1'b0), .pin5(1'b0), .pin6(1'b0), .pin7(1'b1), .pin8(1'b0),
    .pin9(nLD_S), .pin10(1'b1), .pin11(S[3]), .pin12(S[2]), .pin13(S[1]), .pin14(S[0]), .pin16(1'b1));  // open: pin15
  PullUp #(.Bits(8)) pullup_1 (.out(BUS));
  _7400 _7400_1 (
    .pin1(LD_MEM), .pin2(C_EXEC), .pin3(C_nLD_MEM), .pin4(C4_ALU_OP4_LD_IO), .pin5(nLD_C), .pin6(nLD_IO),
    .pin7(1'b0), .pin8(nLD_S), .pin9(nLD_C), .pin10(C2_LD_S), .pin11(nLD_O), .pin12(C1_LD_O), .pin13(nLD_C),
    .pin14(1'b1));
  _7400 _7400_2 (
    .pin1(nLD_C), .pin2(C3_LD_RS), .pin3(nLD_RS), .pin4(A[15]), .pin5(A[15]), .pin6(nA15_nEN_RAM),
    .pin7(1'b0), .pin8(nHALT), .pin9(C5_LS_ALU_Q_HALT), .pin10(nLD_C), .pin12(1'b1), .pin13(1'b1),
    .pin14(1'b1));  // open: pin11
  // Probe on S
  // Probe on BUS
  _74377 u_O (
    .pin1(nLD_O), .pin2(O[0]), .pin3(BUS[0]), .pin4(BUS[1]), .pin5(O[1]), .pin6(O[2]), .pin7(BUS[2]),
    .pin8(BUS[3]), .pin9(O[3]), .pin10(1'b0), .pin11(C_EXEC), .pin12(O[4]), .pin13(BUS[4]), .pin14(BUS[5]),
    .pin15(O[5]), .pin16(O[6]), .pin17(BUS[6]), .pin18(BUS[7]), .pin19(O[7]), .pin20(1'b1));
  _74161 u_ML (
    .pin1(nR), .pin2(C_nEXEC), .pin3(BUS[0]), .pin4(BUS[1]), .pin5(BUS[2]), .pin6(BUS[3]), .pin7(nLD_C),
    .pin8(1'b0), .pin9(nLD_ML), .pin10(C0_CE_M), .pin11(ML[3]), .pin12(ML[2]), .pin13(ML[1]), .pin14(ML[0]),
    .pin15(ML_pin15), .pin16(1'b1));
  _74161 ML_2 (
    .pin1(nR), .pin2(C_nEXEC), .pin3(BUS[4]), .pin4(BUS[5]), .pin5(BUS[6]), .pin6(BUS[7]), .pin7(nLD_C),
    .pin8(1'b0), .pin9(nLD_ML), .pin10(ML_pin15), .pin11(ML[7]), .pin12(ML[6]), .pin13(ML[5]), .pin14(ML[4]),
    .pin15(ML_2_pin15), .pin16(1'b1));
  // Probe on O
  // Probe on ML
  assign BUS = ~nOE_ML ? ML : 8'bz;  // DriverInvSel driverinvsel_1
  _74377 u_C (
    .pin1(nLD_C), .pin2(C_Q0), .pin3(C0_CE_M), .pin4(C1_LD_O), .pin5(C_Q1), .pin6(C_Q2), .pin7(C2_LD_S),
    .pin8(C3_LD_RS), .pin9(C_Q3), .pin10(1'b0), .pin11(C_nEXEC), .pin12(C_Q4_ALU_OP4),
    .pin13(C4_ALU_OP4_LD_IO), .pin14(C5_LS_ALU_Q_HALT), .pin15(C_Q5_ALU_OP5), .pin16(C_Q6_OE_IO),
    .pin17(ALU_Q_IO_OE), .pin18(1'b1), .pin20(1'b1));  // open: pin19
  _74161 u_MH (
    .pin1(nR), .pin2(C_nEXEC), .pin3(BUS[0]), .pin4(BUS[1]), .pin5(BUS[2]), .pin6(BUS[3]), .pin7(nLD_C),
    .pin8(1'b0), .pin9(nLD_MH), .pin10(ML_2_pin15), .pin11(MH[3]), .pin12(MH[2]), .pin13(MH[1]),
    .pin14(MH[0]), .pin15(MH_pin15), .pin16(1'b1));
  _74161 MH_2 (
    .pin1(nR), .pin2(C_nEXEC), .pin3(BUS[4]), .pin4(BUS[5]), .pin5(BUS[6]), .pin6(BUS[7]), .pin7(nLD_C),
    .pin8(1'b0), .pin9(nLD_MH), .pin10(MH_pin15), .pin11(MH[7]), .pin12(MH[6]), .pin13(MH[5]), .pin14(MH[4]),
    .pin15(MH_2_pin15), .pin16(1'b1));
  // Probe on {C_Q3, C_Q2, C_Q1, C_Q0}
  // Probe on MH
  assign BUS = ~nOE_MH ? MH : 8'bz;  // DriverInvSel driverinvsel_2
  _74377 u_LS (
    .pin1(nLD_LS), .pin2(LS[0]), .pin3(BUS[0]), .pin4(BUS[1]), .pin5(LS[1]), .pin6(LS[2]), .pin7(BUS[2]),
    .pin8(BUS[3]), .pin9(LS[3]), .pin10(1'b0), .pin11(C_EXEC), .pin12(LS[4]), .pin13(BUS[4]), .pin14(BUS[5]),
    .pin15(LS[5]), .pin16(LS[6]), .pin17(BUS[6]), .pin18(BUS[7]), .pin19(LS[7]), .pin20(1'b1));
  _74157 AL (
    .pin1(SEL_nM_C), .pin2(ML[0]), .pin3(C_Q0), .pin4(A[0]), .pin5(ML[1]), .pin6(C_Q1), .pin7(A[1]),
    .pin8(1'b0), .pin9(A[2]), .pin10(C_Q2), .pin11(ML[2]), .pin12(A[3]), .pin13(C_Q3), .pin14(ML[3]),
    .pin15(1'b0), .pin16(1'b1));
  _7432 AL_2 (
    .pin1(SEL_nM_C), .pin2(ML[4]), .pin3(A[4]), .pin4(SEL_nM_C), .pin5(ML[5]), .pin6(A[5]), .pin7(1'b0),
    .pin8(A[6]), .pin9(SEL_nM_C), .pin10(ML[6]), .pin11(A[7]), .pin12(SEL_nM_C), .pin13(ML[7]), .pin14(1'b1));
  // Probe on LS
  _74377 u_RS (
    .pin1(nLD_RS), .pin2(RS[0]), .pin3(BUS[0]), .pin4(BUS[1]), .pin5(RS[1]), .pin6(RS[2]), .pin7(BUS[2]),
    .pin8(BUS[3]), .pin9(RS[3]), .pin10(1'b0), .pin11(C_EXEC), .pin12(RS[4]), .pin13(BUS[4]), .pin14(BUS[5]),
    .pin15(RS[5]), .pin16(RS[6]), .pin17(BUS[6]), .pin18(BUS[7]), .pin19(RS[7]), .pin20(1'b1));
  _7432 AH (
    .pin1(SEL_nM_C), .pin2(MH[0]), .pin3(A[8]), .pin4(SEL_nM_C), .pin5(MH[1]), .pin6(A[9]), .pin7(1'b0),
    .pin8(A[10]), .pin9(SEL_nM_C), .pin10(MH[2]), .pin11(A[11]), .pin12(SEL_nM_C), .pin13(MH[3]), .pin14(1'b1));
  _7432 AH_2 (
    .pin1(SEL_nM_C), .pin2(MH[4]), .pin3(A[12]), .pin4(SEL_nM_C), .pin5(MH[5]), .pin6(A[13]), .pin7(1'b0),
    .pin8(A[14]), .pin9(SEL_nM_C), .pin10(MH[6]), .pin11(A[15]), .pin12(SEL_nM_C), .pin13(MH[7]), .pin14(1'b1));
  // Probe on RS
  _74173 F (
    .pin1(1'b0), .pin2(1'b0), .pin3(ZF), .pin4(CF), .pin5(OF), .pin6(SF), .pin7(C_EXEC), .pin8(1'b0),
    .pin9(nLD_LS), .pin10(nOE_ALU), .pin11(ALU_H_Q[3]), .pin12(ALU_Q_OF), .pin13(ALU_Q_CF), .pin14(ALU_Q_ZF),
    .pin15(1'b0), .pin16(1'b1));
  // Probe on A
  // Probe on A[14:0]
  or or_1 (or_1_out, C_nLD_MEM, nA15_nEN_RAM);
  or or_2 (or_2_out, nA15_nEN_RAM, nOE_MEM);
  not not_1 (not_1_out, A[15]);
  or or_3 (or_3_out, nOE_MEM, A[15]);
  RAMAsync #(.AddrBits(15), .Bits(8)) RAM (.A(A[14:0]), .D(BUS), .we(~or_1_out), .Q(RAM_q));
  ROM #(.AddrBits(19), .Bits(8)) PROGRAM (.A({in_2, A[14:0]}), .sel(not_1_out), .D(PROGRAM_d));
  assign BUS = ~or_2_out ? RAM_q : 8'bz;  // DriverInvSel driverinvsel_3
  assign BUS = ~or_3_out ? PROGRAM_d : 8'bz;  // DriverInvSel driverinvsel_4
  ROM #(.AddrBits(17), .Bits(8)) ALU_L (
    .A({C_Q5_ALU_OP5, ALU_H_QC, C_Q4_ALU_OP4, C_Q3, ALU_H_QZ, C_Q2, C_Q1, C_Q0, CF, RS[3:0], LS[3:0]}),
    .sel(1'b1), .D({ALU_L_Q, ALU_Q_IO_OE, ALU_Q_ZF, ALU_L_QC, ALU_L_QZ}));
  ROM #(.AddrBits(17), .Bits(8)) ALU_H (
    .A({C_Q5_ALU_OP5, ALU_L_QC, C_Q4_ALU_OP4, C_Q3, ALU_L_QZ, C_Q2, C_Q1, C_Q0, CF, RS[7:4], LS[7:4]}),
    .sel(1'b1), .D({ALU_H_Q, ALU_Q_OF, ALU_Q_CF, ALU_H_QC, ALU_H_QZ}));
  not not_2 (not_2_out, nLD_PORT0);
  not not_3 (not_3_out, nOE_PORT0);
  Register #(.Bits(8)) register_1 (.D(BUS), .C(C_EXEC), .en(~nLD_PORT1), .Q(register_1_q));
  _74138 IO_PORT_OE (
    .pin1(O[0]), .pin2(O[1]), .pin3(O[2]), .pin4(1'b0), .pin5(1'b0), .pin6(C_Q6_OE_IO), .pin8(1'b0),
    .pin9(IO_PORT_OE_pin9), .pin10(IO_PORT_OE_pin10), .pin11(IO_PORT_OE_pin11), .pin12(IO_PORT_OE_pin12),
    .pin13(IO_PORT_OE_pin13), .pin14(nOE_PORT1), .pin15(nOE_PORT0), .pin16(1'b1));  // open: pin7
  Telnet #(.telnetEscape("false"), .port(2323)) PROGRAM_IO_DEV (
    .in(BUS), .C(C_nEXEC), .wr(not_2_out), .rd(not_3_out), .out(BUS), .av(PROGRAM_IO_DEV_av));
  assign BUS = ~nOE_ALU ? {ALU_H_Q, ALU_L_Q} : 8'bz;  // DriverInvSel driverinvsel_5
  // Probe on ALU_L_Q
  // Probe on ALU_H_Q
  // Probe on register_1_q
  assign BUS = ~nOE_PORT1 ? 8'h10 : 8'bz;  // DriverInvSel driverinvsel_6
  // Probe on {ALU_H_Q, ALU_L_Q}
  // Probe on {ALU_H_Q, ALU_L_Q}
  _74138 IO_PORT_LD (
    .pin1(O[0]), .pin2(O[1]), .pin3(O[2]), .pin4(nLD_IO), .pin5(1'b0), .pin6(1'b1), .pin8(1'b0),
    .pin9(IO_PORT_LD_pin9), .pin10(IO_PORT_LD_pin10), .pin11(IO_PORT_LD_pin11), .pin12(IO_PORT_LD_pin12),
    .pin13(nLD_PORT2), .pin14(nLD_PORT1), .pin15(nLD_PORT0), .pin16(1'b1));  // open: pin7
  not not_4 (not_4_out, nLD_PORT2);
  Terminal TERMINAL (.D(BUS), .C(C_EXEC), .en(not_4_out));

  // Other names for the same wires on the sheet: ALU_Q_SF = ALU_H_Q[3]; A_0__14[14:0] = A[14:0]; A15_nEN_ROM = A[15];
  //   CONST[3:0] = {C_Q3, C_Q2, C_Q1, C_Q0}; LS_L[3:0] = LS[3:0]; LS_Q0 = LS[0]; LS_Q1 = LS[1]; LS_Q2 = LS[2];
  //   LS_Q3 = LS[3]; LS_H[3:0] = LS[7:4]; LS_Q4 = LS[4]; LS_Q5 = LS[5]; LS_Q6 = LS[6]; LS_Q7 = LS[7]; MH_Q0 = MH[0];
  //   MH_Q1 = MH[1]; MH_Q2 = MH[2]; MH_Q3 = MH[3]; MH_Q4 = MH[4]; MH_Q5 = MH[5]; MH_Q6 = MH[6]; MH_Q7 = MH[7];
  //   ML_Q0 = ML[0]; ML_Q1 = ML[1]; ML_Q2 = ML[2]; ML_Q3 = ML[3]; ML_Q4 = ML[4]; ML_Q5 = ML[5]; ML_Q6 = ML[6];
  //   ML_Q7 = ML[7]; O_Q0 = O[0]; O_Q1 = O[1]; O_Q2 = O[2]; O_Q3 = O[3]; O_Q4 = O[4]; O_Q5 = O[5]; O_Q6 = O[6];
  //   O_Q7 = O[7]; RS_L[3:0] = RS[3:0]; RS_Q0 = RS[0]; RS_Q1 = RS[1]; RS_Q2 = RS[2]; RS_Q3 = RS[3];
  //   RS_H[3:0] = RS[7:4]; RS_Q4 = RS[4]; RS_Q5 = RS[5]; RS_Q6 = RS[6]; RS_Q7 = RS[7]; S_Q0 = S[0]; S_Q1 = S[1];
  //   S_Q2 = S[2]; S_Q3 = S[3]

  // Notes on the sheet:
  //   C: Hz: 1000
  //   in_2: default 1
  //   contents of CTRL_L (hex, n*v repeats v):
  //   1024*df,1024*dd,1024*df,1024*dd,1024*df,1024*58,1024*df,1024*58
  //   ,1024*df,1024*dd,1024*df,1024*dd,1024*df,1024*58,1024*df,1024*58
  //   ,1024*df,1024*d8,1024*df,1024*d8,1024*df,1024*d8,1024*df,1024*d8
  //   ,1024*df,1024*d8,1024*df,1024*d8,1024*df,1024*d8,1024*df,1024*d8
  //   ,1024*df,1024*cc,1024*df,1024*cc,1024*df,1024*f8,1024*df,1024*f8
  //   ,1024*df,1024*cc,1024*df,1024*cc,1024*df,1024*f8,1024*df,1024*f8
  //   ,1024*df,1024*d8,1024*df,1024*d8,1024*df,1024*d8,1024*df,1024*d8
  //   ,1024*df,1024*d8,1024*df,1024*d8,1024*df,1024*d8,1024*df,1024*d8
  //   ,1024*df,1024*59,1024*df,1024*59,1024*df,1024*cc,1024*df,1024*cc
  //   ,1024*df,1024*59,1024*df,1024*59,1024*df,1024*cc,1024*df,1024*cc
  //   ,1024*df,1024*d8,1024*df,1024*d8,1024*df,1024*d8,1024*df,1024*d8
  //   ,1024*df,1024*d8,1024*df,1024*d8,1024*df,1024*d8,1024*df,1024*d8
  //   ,1024*df,1024*f8,1024*df,1024*f8,1024*df,1024*d8,1024*df,1024*d8
  //   ,1024*df,1024*f8,1024*df,1024*f8,1024*df,1024*d8,1024*df,1024*d8
  //   ,1024*df,1024*d8,1024*df,1024*d8,1024*df,1024*d8,1024*df,1024*d8
  //   ,1024*df,1024*d8,1024*df,1024*d8,1024*df,1024*d8,1024*df,1024*d8
  //   contents of CTRL_H (hex, n*v repeats v):
  //   1024*df,1024*dd,1024*df,1024*dd,1024*df,1024*58,1024*df,1024*58
  //   ,1024*df,1024*dd,1024*df,1024*dd,1024*df,1024*58,1024*df,1024*58
  //   ,1024*df,1024*d8,1024*df,1024*d8,1024*df,1024*d8,1024*df,1024*d8
  //   ,1024*df,1024*d8,1024*df,1024*d8,1024*df,1024*d8,1024*df,1024*d8
  //   ,1024*df,1024*cc,1024*df,1024*cc,1024*df,1024*f8,1024*df,1024*f8
  //   ,1024*df,1024*cc,1024*df,1024*cc,1024*df,1024*f8,1024*df,1024*f8
  //   ,1024*df,1024*d8,1024*df,1024*d8,1024*df,1024*d8,1024*df,1024*d8
  //   ,1024*df,1024*d8,1024*df,1024*d8,1024*df,1024*d8,1024*df,1024*d8
  //   ,1024*df,1024*59,1024*df,1024*59,1024*df,1024*cc,1024*df,1024*cc
  //   ,1024*df,1024*59,1024*df,1024*59,1024*df,1024*cc,1024*df,1024*cc
  //   ,1024*df,1024*d8,1024*df,1024*d8,1024*df,1024*d8,1024*df,1024*d8
  //   ,1024*df,1024*d8,1024*df,1024*d8,1024*df,1024*d8,1024*df,1024*d8
  //   ,1024*df,1024*f8,1024*df,1024*f8,1024*df,1024*d8,1024*df,1024*d8
  //   ,1024*df,1024*f8,1024*df,1024*f8,1024*df,1024*d8,1024*df,1024*d8
  //   ,1024*df,1024*d8,1024*df,1024*d8,1024*df,1024*d8,1024*df,1024*d8
  //   ,1024*df,1024*d8,1024*df,1024*d8,1024*df,1024*d8,1024*df,1024*d8
  //   PROGRAM loads software_rom.bin
  //   contents of ALU_L (hex, n*v repeats v):
  //   4*10,4*f2,1,5,1,5,248*10,4*f2,4*10,244*20,4*10,4*f2,4*20,244*30
  //   ,4*10,4*f2,4*30,244*40,4*10,4*f2,4*40,244*50,4*10,4*f2,4*50,244*60
  //   ,4*10,4*f2,4*60,244*70,4*10,4*f2,4*70,244*88,4*10,4*f2,4*80,244*98
  //   ,4*10,4*f2,4*90,244*a8,4*10,4*f2,4*a0,244*b8,4*10,4*f2,4*b0,244*c8
  //   ,4*10,4*f2,4*c0,244*d8,4*10,4*f2,4*d0,244*e8,4*10,4*f2,4*e0,244*f8
  //   ,4*10,4*f2,4*f0,244*7,4*10,4*f2,1,5,1,5,248*10,4*f2,4*10,244*20
  //   ,4*10,4*f2,4*20,244*30,4*10,4*f2,4*30,244*40,4*10,4*f2,4*40,244*50
  //   ,4*10,4*f2,4*50,244*60,4*10,4*f2,4*60,244*70,4*10,4*f2,4*70,244*88
  //   ,4*10,4*f2,4*80,244*98,4*10,4*f2,4*90,244*a8,4*10,4*f2,4*a0,244*b8
  //   ,4*10,4*f2,4*b0,244*c8,4*10,4*f2,4*c0,244*d8,4*10,4*f2,4*d0,244*e8
  //   ,4*10,4*f2,4*e0,244*f8,4*10,4*f2,4*f0,244*7,4*20,1,5,1,5,4*10
  //   ,248*20,1,5,1,5,4*20,244*30,4*20,1,5,1,5,4*30,244*40,4*20,1,5
  //   ,1,5,4*40,244*50,4*20,1,5,1,5,4*50,244*60,4*20,1,5,1,5,4*60,244*70
  //   ,4*20,1,5,1,5,4*70,244*88,4*20,1,5,1,5,4*80,244*98,4*20,1,5,1
  //   ,5,4*90,244*a8,4*20,1,5,1,5,4*a0,244*b8,4*20,1,5,1,5,4*b0,244*c8
  //   ,4*20,1,5,1,5,4*c0,244*d8,4*20,1,5,1,5,4*d0,244*e8,4*20,1,5,1
  //   ,5,4*e0,244*f8,4*20,1,5,1,5,4*f0,244*7,4*20,1,5,1,5,3,7,3,7,244*16
  //   ,4*20,1,5,1,5,4*10,248*20,1,5,1,5,4*20,244*30,4*20,1,5,1,5,4*30
  //   ,244*40,4*20,1,5,1,5,4*40,244*50,4*20,1,5,1,5,4*50,244*60,4*20
  //   ,1,5,1,5,4*60,244*70,4*20,1,5,1,5,4*70,244*88,4*20,1,5,1,5,4*80
  //   ,244*98,4*20,1,5,1,5,4*90,244*a8,4*20,1,5,1,5,4*a0,244*b8,4*20
  //   ,1,5,1,5,4*b0,244*c8,4*20,1,5,1,5,4*c0,244*d8,4*20,1,5,1,5,4*d0
  //   ,244*e8,4*20,1,5,1,5,4*e0,244*f8,4*20,1,5,1,5,4*f0,244*7,4*20
  //   ,1,5,1,5,3,7,3,7,244*16,4*30,4*10,4*20,248*30,4*10,4*30,244*40
  //   ,4*30,4*10,4*40,244*50,4*30,4*10,4*50,244*60,4*30,4*10,4*60,244*70
  //   ,4*30,4*10,4*70,244*88,4*30,4*10,4*80,244*98,4*30,4*10,4*90,244*a8
  //   ,4*30,4*10,4*a0,244*b8,4*30,4*10,4*b0,244*c8,4*30,4*10,4*c0,244*d8
  //   ,4*30,4*10,4*d0,244*e8,4*30,4*10,4*e0,244*f8,4*30,4*10,4*f0,244*7
  //   ,4*30,4*10,3,7,3,7,244*16,4*30,4*10,4*12,244*26,4*30,4*10,4*20
  //   ,248*30,4*10,4*30,244*40,4*30,4*10,4*40,244*50,4*30,4*10,4*50
  //   ,244*60,4*30,4*10,4*60,244*70,4*30,4*10,4*70,244*88,4*30,4*10
  //   ,4*80,244*98,4*30,4*10,4*90,244*a8,4*30,4*10,4*a0,244*b8,4*30
  //   ,4*10,4*b0,244*c8,4*30,4*10,4*c0,244*d8,4*30,4*10,4*d0,244*e8
  //   ,4*30,4*10,4*e0,244*f8,4*30,4*10,4*f0,244*7,4*30,4*10,3,7,3,7
  //   ,244*16,4*30,4*10,4*12,244*26,4*40,4*20,4*30,248*40,4*20,4*40
  //   ,244*50,4*40,4*20,4*50,244*60,4*40,4*20,4*60,244*70,4*40,4*20
  //   ,4*70,244*88,4*40,4*20,4*80,244*98,4*40,4*20,4*90,244*a8,4*40
  //   ,4*20,4*a0,244*b8,4*40,4*20,4*b0,244*c8,4*40,4*20,4*c0,244*d8
  //   ,4*40,4*20,4*d0,244*e8,4*40,4*20,4*e0,244*f8,4*40,4*20,4*f0,244*7
  //   ,4*40,4*20,3,7,3,7,244*16,4*40,4*20,4*12,244*26,4*40,4*20,4*22
  //   ,244*36,4*40,4*20,4*30,248*40,4*20,4*40,244*50,4*40,4*20,4*50
  //   ,244*60,4*40,4*20,4*60,244*70,4*40,4*20,4*70,244*88,4*40,4*20
  //   ,4*80,244*98,4*40,4*20,4*90,244*a8,4*40,4*20,4*a0,244*b8,4*40
  //   ,4*20,4*b0,244*c8,4*40,4*20,4*c0,244*d8,4*40,4*20,4*d0,244*e8
  //   ,4*40,4*20,4*e0,244*f8,4*40,4*20,4*f0,244*7,4*40,4*20,3,7,3,7
  //   ,244*16,4*40,4*20,4*12,244*26,4*40,4*20,4*22,244*36,4*50,4*30
  //   ,4*40,248*50,4*30,4*50,244*60,4*50,4*30,4*60,244*70,4*50,4*30
  //   ,4*70,244*88,4*50,4*30,4*80,244*98,4*50,4*30,4*90,244*a8,4*50
  //   ,4*30,4*a0,244*b8,4*50,4*30,4*b0,244*c8,4*50,4*30,4*c0,244*d8
  //   ,4*50,4*30,4*d0,244*e8,4*50,4*30,4*e0,244*f8,4*50,4*30,4*f0,244*7
  //   ,4*50,4*30,3,7,3,7,244*16,4*50,4*30,4*12,244*26,4*50,4*30,4*22
  //   ,244*36,4*50,4*30,4*32,244*46,4*50,4*30,4*40,248*50,4*30,4*50
  //   ,244*60,4*50,4*30,4*60,244*70,4*50,4*30,4*70,244*88,4*50,4*30
  //   ,4*80,244*98,4*50,4*30,4*90,244*a8,4*50,4*30,4*a0,244*b8,4*50
  //   ,4*30,4*b0,244*c8,4*50,4*30,4*c0,244*d8,4*50,4*30,4*d0,244*e8
  //   ,4*50,4*30,4*e0,244*f8,4*50,4*30,4*f0,244*7,4*50,4*30,3,7,3,7
  //   ,244*16,4*50,4*30,4*12,244*26,4*50,4*30,4*22,244*36,4*50,4*30
  //   ,4*32,244*46,4*60,4*40,4*50,248*60,4*40,4*60,244*70,4*60,4*40
  //   ,4*70,244*88,4*60,4*40,4*80,244*98,4*60,4*40,4*90,244*a8,4*60
  //   ,4*40,4*a0,244*b8,4*60,4*40,4*b0,244*c8,4*60,4*40,4*c0,244*d8
  //   ,4*60,4*40,4*d0,244*e8,4*60,4*40,4*e0,244*f8,4*60,4*40,4*f0,244*7
  //   ,4*60,4*40,3,7,3,7,244*16,4*60,4*40,4*12,244*26,4*60,4*40,4*22
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  //   contents of ALU_H (hex, n*v repeats v):
  //   1,1,10,10,1,1,f2,f2,1,1,246*10,1,1,10,10,1,1,f2,f2,10,10,246*20
  //   ,1,1,10,10,1,1,f2,f2,20,20,246*30,1,1,10,10,1,1,f2,f2,30,30,246*40
  //   ,1,1,10,10,1,1,f2,f2,40,40,246*50,1,1,10,10,1,1,f2,f2,50,50,246*60
  //   ,1,1,10,10,1,1,f2,f2,60,60,246*70,1,1,10,10,1,1,f2,f2,70,70,246*88
  //   ,1,1,10,10,1,1,f2,f2,88,88,246*98,1,1,10,10,1,1,f2,f2,98,98,246*a8
  //   ,1,1,10,10,1,1,f2,f2,a8,a8,246*b8,1,1,10,10,1,1,f2,f2,b8,b8,246*c8
  //   ,1,1,10,10,1,1,f2,f2,c8,c8,246*d8,1,1,10,10,1,1,f2,f2,d8,d8,246*e8
  //   ,1,1,10,10,1,1,f2,f2,e8,e8,246*f8,1,1,10,10,1,1,f2,f2,f8,f8,246*7
  //   ,5,5,14,14,5,5,f6,f6,1,1,246*10,5,5,14,14,5,5,f6,f6,10,10,246*20
  //   ,5,5,14,14,5,5,f6,f6,20,20,246*30,5,5,14,14,5,5,f6,f6,30,30,246*40
  //   ,5,5,14,14,5,5,f6,f6,40,40,246*50,5,5,14,14,5,5,f6,f6,50,50,246*60
  //   ,5,5,14,14,5,5,f6,f6,60,60,246*70,5,5,14,14,5,5,f6,f6,70,70,246*88
  //   ,5,5,14,14,5,5,f6,f6,88,88,246*98,5,5,14,14,5,5,f6,f6,98,98,246*a8
  //   ,5,5,14,14,5,5,f6,f6,a8,a8,246*b8,5,5,14,14,5,5,f6,f6,b8,b8,246*c8
  //   ,5,5,14,14,5,5,f6,f6,c8,c8,246*d8,5,5,14,14,5,5,f6,f6,d8,d8,246*e8
  //   ,5,5,14,14,5,5,f6,f6,e8,e8,246*f8,5,5,14,14,5,5,f6,f6,f8,f8,246*7
  //   ,10,10,20,20,10,10,1,1,10,10,246*20,10,10,20,20,10,10,1,1,20,20
  //   ,246*30,10,10,20,20,10,10,1,1,30,30,246*40,10,10,20,20,10,10,1,1
  //   ,40,40,246*50,10,10,20,20,10,10,1,1,50,50,246*60,10,10,20,20,10,10
  //   ,1,1,60,60,246*70,10,10,20,20,10,10,1,1,70,70,246*88,10,10,20,20
  //   ,10,10,1,1,88,88,246*98,10,10,20,20,10,10,1,1,98,98,246*a8,10,10
  //   ,20,20,10,10,1,1,a8,a8,246*b8,10,10,20,20,10,10,1,1,b8,b8,246*c8
  //   ,10,10,20,20,10,10,1,1,c8,c8,246*d8,10,10,20,20,10,10,1,1,d8,d8
  //   ,246*e8,10,10,20,20,10,10,1,1,e8,e8,246*f8,10,10,20,20,10,10,1,1
  //   ,f8,f8,246*7,10,10,20,20,10,10,1,1,7,7,246*16,14,14,24,24,14,14
  //   ,5,5,10,10,246*20,14,14,24,24,14,14,5,5,20,20,246*30,14,14,24,24
  //   ,14,14,5,5,30,30,246*40,14,14,24,24,14,14,5,5,40,40,246*50,14,14
  //   ,24,24,14,14,5,5,50,50,246*60,14,14,24,24,14,14,5,5,60,60,246*70
  //   ,14,14,24,24,14,14,5,5,70,70,246*88,14,14,24,24,14,14,5,5,88,88
  //   ,246*98,14,14,24,24,14,14,5,5,98,98,246*a8,14,14,24,24,14,14,5,5
  //   ,a8,a8,246*b8,14,14,24,24,14,14,5,5,b8,b8,246*c8,14,14,24,24,14,14
  //   ,5,5,c8,c8,246*d8,14,14,24,24,14,14,5,5,d8,d8,246*e8,14,14,24,24
  //   ,14,14,5,5,e8,e8,246*f8,14,14,24,24,14,14,5,5,f8,f8,246*7,14,14
  //   ,24,24,14,14,5,5,7,7,246*16,20,20,30,30,20,20,10,10,20,20,246*30
  //   ,20,20,30,30,20,20,10,10,30,30,246*40,20,20,30,30,20,20,10,10
  //   ,40,40,246*50,20,20,30,30,20,20,10,10,50,50,246*60,20,20,30,30
  //   ,20,20,10,10,60,60,246*70,20,20,30,30,20,20,10,10,70,70,246*88
  //   ,20,20,30,30,20,20,10,10,88,88,246*98,20,20,30,30,20,20,10,10
  //   ,98,98,246*a8,20,20,30,30,20,20,10,10,a8,a8,246*b8,20,20,30,30
  //   ,20,20,10,10,b8,b8,246*c8,20,20,30,30,20,20,10,10,c8,c8,246*d8
  //   ,20,20,30,30,20,20,10,10,d8,d8,246*e8,20,20,30,30,20,20,10,10
  //   ,e8,e8,246*f8,20,20,30,30,20,20,10,10,f8,f8,246*7,20,20,30,30
  //   ,20,20,10,10,7,7,246*16,20,20,30,30,20,20,10,10,16,16,246*26,24,24
  //   ,34,34,24,24,14,14,20,20,246*30,24,24,34,34,24,24,14,14,30,30
  //   ,246*40,24,24,34,34,24,24,14,14,40,40,246*50,24,24,34,34,24,24
  //   ,14,14,50,50,246*60,24,24,34,34,24,24,14,14,60,60,246*70,24,24
  //   ,34,34,24,24,14,14,70,70,246*88,24,24,34,34,24,24,14,14,88,88
  //   ,246*98,24,24,34,34,24,24,14,14,98,98,246*a8,24,24,34,34,24,24
  //   ,14,14,a8,a8,246*b8,24,24,34,34,24,24,14,14,b8,b8,246*c8,24,24
  //   ,34,34,24,24,14,14,c8,c8,246*d8,24,24,34,34,24,24,14,14,d8,d8
  //   ,246*e8,24,24,34,34,24,24,14,14,e8,e8,246*f8,24,24,34,34,24,24
  //   ,14,14,f8,f8,246*7,24,24,34,34,24,24,14,14,7,7,246*16,24,24,34,34
  //   ,24,24,14,14,16,16,246*26,30,30,40,40,30,30,20,20,30,30,246*40
  //   ,30,30,40,40,30,30,20,20,40,40,246*50,30,30,40,40,30,30,20,20
  //   ,50,50,246*60,30,30,40,40,30,30,20,20,60,60,246*70,30,30,40,40
  //   ,30,30,20,20,70,70,246*88,30,30,40,40,30,30,20,20,88,88,246*98
  //   ,30,30,40,40,30,30,20,20,98,98,246*a8,30,30,40,40,30,30,20,20
  //   ,a8,a8,246*b8,30,30,40,40,30,30,20,20,b8,b8,246*c8,30,30,40,40
  //   ,30,30,20,20,c8,c8,246*d8,30,30,40,40,30,30,20,20,d8,d8,246*e8
  //   ,30,30,40,40,30,30,20,20,e8,e8,246*f8,30,30,40,40,30,30,20,20
  //   ,f8,f8,246*7,30,30,40,40,30,30,20,20,7,7,246*16,30,30,40,40,30,30
  //   ,20,20,16,16,246*26,30,30,40,40,30,30,20,20,26,26,246*36,34,34
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endmodule
